// Logisim project alu8bit.circ as structural Verilog: 13 circuits, main circuit main
module main (
  input  Cin,
  input  A,
  input  in_3,
  input  in_4,
  input  in_5,
  input  in_6,
  input  in_7,
  input  in_8,
  input  in_9,
  input  B,
  input  in_11,
  input  in_12,
  input  in_13,
  input  in_14,
  input  in_15,
  input  in_16,
  input  in_17,
  input  D,
  input  in_19,
  output O,
  output out_21,
  output out_22,
  output out_23,
  output out_24,
  output out_25,
  output out_26,
  output out_27,
  output Cout,
  output SE
);

  ALU_8bit_implemented alu_8bit_implemented_1 (
    .D1(in_19), .D2(D), .A1(A), .A2(in_3), .A3(in_4), .A4(in_5), .A5(in_6), .A6(in_7), .A7(in_8), .A8(in_9),
    .B1(B), .B2(in_11), .B3(in_12), .B4(in_13), .B5(in_14), .B6(in_15), .B7(in_16), .B8(in_17), .Cin(Cin),
    .O1(O), .O2(out_21), .O3(out_22), .O4(out_23), .O5(out_24), .O6(out_25), .O7(out_26), .O8(out_27),
    .Cout(Cout), .SO(SE));
endmodule

module Decoder_2bit_implemented (
  input  D1,
  input  D2,
  output D00,
  output D01,
  output D10,
  output D11
);

  wire not_1_out, not_2_out;

  not not_1 (not_1_out, D1);
  not not_2 (not_2_out, D2);
  and and_1 (D00, not_1_out, not_2_out);
  and and_2 (D01, not_1_out, D2);
  and and_3 (D10, D1, not_2_out);
  and and_4 (D11, D1, D2);
endmodule

module ALU_1bit (
  input  A,
  input  B,
  input  D1,
  input  D2,
  input  Cin,
  output O,
  output Cout
);

  wire and_1_out, and_2_out, and_3_out, and_4_out, and_5_out, and_6_out, and_7_out, and_8_out, and_9_out,
       and_10_out, not_1_out, not_2_out, not_3_out, or_1_out, or_2_out, or_3_out, xor_1_out, xor_2_out,
       xor_3_out;

  not not_1 (not_1_out, D1);
  not not_2 (not_2_out, D2);
  not not_3 (not_3_out, A);
  and and_1 (and_1_out, A, B);
  or or_1 (or_1_out, A, B);
  and and_2 (and_2_out, not_1_out, not_2_out);
  and and_3 (and_3_out, not_1_out, D2);
  and and_4 (and_4_out, D1, not_2_out);
  and and_5 (and_5_out, D1, D2);
  and and_6 (and_6_out, not_3_out, and_2_out);
  and and_7 (and_7_out, and_1_out, and_3_out);
  and and_8 (and_8_out, or_1_out, and_4_out);
  xor xor_1 (xor_1_out, A, B);
  or or_2 (or_2_out, and_6_out, and_7_out);
  xor xor_2 (xor_2_out, xor_1_out, Cin);
  and and_9 (and_9_out, xor_1_out, Cin);
  or or_3 (or_3_out, or_2_out, and_10_out);
  and and_10 (and_10_out, and_5_out, xor_2_out);
  xor xor_3 (xor_3_out, and_9_out, and_1_out);
  or or_4 (O, or_3_out, and_8_out);
  and and_11 (Cout, and_5_out, xor_3_out);
endmodule

module ALU_1bit_implemented (
  input  A,
  input  B,
  input  Cin,
  input  D00,
  input  D01,
  input  D10,
  input  D11,
  output O,
  output Cout
);

  wire and_1_out, and_2_out, and_3_out, and_4_out, and_5_out, and_6_out, not_1_out, or_1_out, or_2_out,
       or_3_out, xor_1_out, xor_2_out, xor_3_out;

  not not_1 (not_1_out, A);
  and and_1 (and_1_out, A, B);
  or or_1 (or_1_out, A, B);
  and and_2 (and_2_out, not_1_out, D00);
  and and_3 (and_3_out, and_1_out, D01);
  and and_4 (and_4_out, or_1_out, D10);
  xor xor_1 (xor_1_out, A, B);
  or or_2 (or_2_out, and_2_out, and_3_out);
  xor xor_2 (xor_2_out, xor_1_out, Cin);
  and and_5 (and_5_out, xor_1_out, Cin);
  or or_3 (or_3_out, or_2_out, and_6_out);
  and and_6 (and_6_out, D11, xor_2_out);
  xor xor_3 (xor_3_out, and_5_out, and_1_out);
  or or_4 (O, or_3_out, and_4_out);
  and and_7 (Cout, D11, xor_3_out);
endmodule

module ALU_2bit_implemented (
  input  A1,
  input  B1,
  input  A2,
  input  B2,
  input  Cin,
  input  D00,
  input  D01,
  input  D10,
  input  D11,
  output O1,
  output O2,
  output Cout
);

  wire alu_1bit_implemented_2_cout;

  ALU_1bit_implemented alu_1bit_implemented_1 (
    .A(A1), .B(B1), .Cin(alu_1bit_implemented_2_cout), .D00(D00), .D01(D01), .D10(D10), .D11(D11), .O(O1),
    .Cout(Cout));
  ALU_1bit_implemented alu_1bit_implemented_2 (
    .A(A2), .B(B2), .Cin(Cin), .D00(D00), .D01(D01), .D10(D10), .D11(D11), .O(O2),
    .Cout(alu_1bit_implemented_2_cout));
endmodule

module ALU_2bit_most_significant_implemented (
  input  A1,
  input  B1,
  input  A2,
  input  B2,
  input  Cin,
  input  D00,
  input  D01,
  input  D10,
  input  D11,
  output O1,
  output O2,
  output Cout,
  output SE
);

  wire alu_1bit_implemented_2_cout;

  ALU_1bit_implemented alu_1bit_implemented_1 (
    .A(A1), .B(B1), .Cin(alu_1bit_implemented_2_cout), .D00(D00), .D01(D01), .D10(D10), .D11(D11), .O(O1),
    .Cout(Cout));
  ALU_1bit_implemented alu_1bit_implemented_2 (
    .A(A2), .B(B2), .Cin(Cin), .D00(D00), .D01(D01), .D10(D10), .D11(D11), .O(O2),
    .Cout(alu_1bit_implemented_2_cout));
  xor xor_1 (SE, Cout, alu_1bit_implemented_2_cout);
endmodule

module ALU_8bit_implemented (
  input  D1,
  input  D2,
  input  A1,
  input  A2,
  input  A3,
  input  A4,
  input  A5,
  input  A6,
  input  A7,
  input  A8,
  input  B1,
  input  B2,
  input  B3,
  input  B4,
  input  B5,
  input  B6,
  input  B7,
  input  B8,
  input  Cin,
  output O1,
  output O2,
  output O3,
  output O4,
  output O5,
  output O6,
  output O7,
  output O8,
  output Cout,
  output SO
);

  wire alu_2bit_implemented_1_cout, alu_2bit_implemented_2_cout, alu_2bit_implemented_3_cout,
       decoder_2bit_implemented_1_d00, decoder_2bit_implemented_1_d01, decoder_2bit_implemented_1_d10,
       decoder_2bit_implemented_1_d11;

  Decoder_2bit_implemented decoder_2bit_implemented_1 (
    .D1(D1), .D2(D2), .D00(decoder_2bit_implemented_1_d00), .D01(decoder_2bit_implemented_1_d01),
    .D10(decoder_2bit_implemented_1_d10), .D11(decoder_2bit_implemented_1_d11));
  ALU_2bit_most_significant_implemented alu_2bit_most_significant_implemented_1 (
    .A1(A1), .B1(B1), .A2(A2), .B2(B2), .Cin(alu_2bit_implemented_1_cout),
    .D00(decoder_2bit_implemented_1_d00), .D01(decoder_2bit_implemented_1_d01),
    .D10(decoder_2bit_implemented_1_d10), .D11(decoder_2bit_implemented_1_d11), .O1(O1), .O2(O2),
    .Cout(Cout), .SE(SO));
  ALU_2bit_implemented alu_2bit_implemented_1 (
    .A1(A3), .B1(B3), .A2(A4), .B2(B4), .Cin(alu_2bit_implemented_2_cout),
    .D00(decoder_2bit_implemented_1_d00), .D01(decoder_2bit_implemented_1_d01),
    .D10(decoder_2bit_implemented_1_d10), .D11(decoder_2bit_implemented_1_d11), .O1(O3), .O2(O4),
    .Cout(alu_2bit_implemented_1_cout));
  ALU_2bit_implemented alu_2bit_implemented_2 (
    .A1(A5), .B1(B5), .A2(A6), .B2(B6), .Cin(alu_2bit_implemented_3_cout),
    .D00(decoder_2bit_implemented_1_d00), .D01(decoder_2bit_implemented_1_d01),
    .D10(decoder_2bit_implemented_1_d10), .D11(decoder_2bit_implemented_1_d11), .O1(O5), .O2(O6),
    .Cout(alu_2bit_implemented_2_cout));
  ALU_2bit_implemented alu_2bit_implemented_3 (
    .A1(A7), .B1(B7), .A2(A8), .B2(B8), .Cin(Cin), .D00(decoder_2bit_implemented_1_d00),
    .D01(decoder_2bit_implemented_1_d01), .D10(decoder_2bit_implemented_1_d10),
    .D11(decoder_2bit_implemented_1_d11), .O1(O7), .O2(O8), .Cout(alu_2bit_implemented_3_cout));
endmodule

module logic_section (
  input  A,
  input  B,
  output not_A,
  output A_and_B,
  output A_or_B
);

  not not_1 (not_A, A);
  and and_1 (A_and_B, A, B);
  or or_1 (A_or_B, A, B);
endmodule

module full_adder (
  input  A,
  input  B,
  input  Carry_in,
  output Sum,
  output Carry_Out
);

  wire and_1_out, and_2_out, xor_1_out;

  xor xor_1 (xor_1_out, A, B);
  and and_1 (and_1_out, A, B);
  xor xor_2 (Sum, xor_1_out, Carry_in);
  and and_2 (and_2_out, xor_1_out, Carry_in);
  xor xor_3 (Carry_Out, and_2_out, and_1_out);
endmodule

module output_section (
  input  not_A,
  input  D00,
  input  A_and_B,
  input  D01,
  input  A_or_B,
  input  D10,
  input  A_sum_B,
  input  D11,
  input  Carry_Out,
  output O,
  output Cout
);

  wire and_1_out, and_2_out, and_3_out, and_4_out, or_1_out, or_2_out;

  and and_1 (and_1_out, not_A, D00);
  and and_2 (and_2_out, A_and_B, D01);
  and and_3 (and_3_out, A_or_B, D10);
  and and_4 (and_4_out, A_sum_B, D11);
  and and_5 (Cout, Carry_Out, D11);
  or or_1 (or_1_out, and_1_out, and_2_out);
  or or_2 (or_2_out, or_1_out, and_3_out);
  or or_3 (O, or_2_out, and_4_out);
endmodule

module ALU_1_bit_modular_implemented (
  input  A,
  input  B,
  input  Cin,
  input  D1,
  input  D2,
  output O,
  output Cout
);

  wire decoder_2bit_implemented_1_d00, decoder_2bit_implemented_1_d01, decoder_2bit_implemented_1_d10,
       decoder_2bit_implemented_1_d11, full_adder_1_carry_out, full_adder_1_sum, logic_section_1_a_and_b,
       logic_section_1_a_or_b, logic_section_1_not_a;

  logic_section logic_section_1 (
    .A(A), .B(B), .not_A(logic_section_1_not_a), .A_and_B(logic_section_1_a_and_b),
    .A_or_B(logic_section_1_a_or_b));
  full_adder full_adder_1 (.A(A), .B(B), .Carry_in(Cin), .Sum(full_adder_1_sum), .Carry_Out(full_adder_1_carry_out));
  Decoder_2bit_implemented decoder_2bit_implemented_1 (
    .D1(D1), .D2(D2), .D00(decoder_2bit_implemented_1_d00), .D01(decoder_2bit_implemented_1_d01),
    .D10(decoder_2bit_implemented_1_d10), .D11(decoder_2bit_implemented_1_d11));
  output_section output_section_1 (
    .not_A(logic_section_1_not_a), .D00(decoder_2bit_implemented_1_d00), .A_and_B(logic_section_1_a_and_b),
    .D01(decoder_2bit_implemented_1_d01), .A_or_B(logic_section_1_a_or_b),
    .D10(decoder_2bit_implemented_1_d10), .A_sum_B(full_adder_1_sum), .D11(decoder_2bit_implemented_1_d11),
    .Carry_Out(full_adder_1_carry_out), .O(O), .Cout(Cout));
endmodule

module stack_error_section (
  input  Cin,
  input  Cout,
  output SE
);

  xor xor_1 (SE, Cin, Cout);
endmodule

module ALU_1bit_modular_most_significant_implemented (
  input  A,
  input  B,
  input  Cin,
  input  D1,
  input  D2,
  output O,
  output Cout,
  output SE
);

  wire decoder_2bit_implemented_1_d00, decoder_2bit_implemented_1_d01, decoder_2bit_implemented_1_d10,
       decoder_2bit_implemented_1_d11, full_adder_1_sum, logic_section_1_a_and_b, logic_section_1_a_or_b,
       logic_section_1_not_a;

  logic_section logic_section_1 (
    .A(A), .B(B), .not_A(logic_section_1_not_a), .A_and_B(logic_section_1_a_and_b),
    .A_or_B(logic_section_1_a_or_b));
  full_adder full_adder_1 (.A(A), .B(B), .Carry_in(Cin), .Sum(full_adder_1_sum), .Carry_Out(Cout));
  Decoder_2bit_implemented decoder_2bit_implemented_1 (
    .D1(D1), .D2(D2), .D00(decoder_2bit_implemented_1_d00), .D01(decoder_2bit_implemented_1_d01),
    .D10(decoder_2bit_implemented_1_d10), .D11(decoder_2bit_implemented_1_d11));
  output_section output_section_1 (
    .not_A(logic_section_1_not_a), .D00(decoder_2bit_implemented_1_d00), .A_and_B(logic_section_1_a_and_b),
    .D01(decoder_2bit_implemented_1_d01), .A_or_B(logic_section_1_a_or_b),
    .D10(decoder_2bit_implemented_1_d10), .A_sum_B(full_adder_1_sum), .D11(decoder_2bit_implemented_1_d11),
    .O(O));  // open: Carry_Out, Cout
  stack_error_section stack_error_section_1 (.Cin(Cin), .Cout(Cout), .SE(SE));
endmodule
